// Logisim project shiftbzdddd.circ as structural Verilog: 1 circuit, main circuit main
module main (
  input  [1:0] S1_S0,
  input  B_IN,
  output A7,
  output A6,
  output A5,
  output A4,
  output A3,
  output A2,
  output A1,
  output A0,
  output B_OUT
);

  wire CLK_out, multiplexer_1_out, multiplexer_2_out, multiplexer_3_out, multiplexer_4_out,
       multiplexer_5_out, multiplexer_6_out, multiplexer_7_out, multiplexer_8_out, multiplexer_9_out,
       multiplexer_10_out;

  D_Flip_Flop #(.trigger("falling")) d_ff_1 (.D(multiplexer_1_out), .clk(CLK_out), .Q(A7));  // open: Qn, preset, reset
  Multiplexer #(.select(2)) multiplexer_1 (
    .in1(A6), .in2(multiplexer_2_out), .in3(A0), .out(multiplexer_1_out), .sel(S1_S0));  // open: in0
  Multiplexer #(.select(2)) multiplexer_2 (.in2(B_IN), .out(multiplexer_2_out), .sel(S1_S0));  // open: in0, in1, in3
  Multiplexer #(.select(2)) multiplexer_3 (
    .in1(A5), .in2(A7), .in3(A7), .out(multiplexer_3_out), .sel(S1_S0));  // open: in0
  D_Flip_Flop #(.trigger("falling")) d_ff_2 (.D(multiplexer_3_out), .clk(CLK_out), .Q(A6));  // open: Qn, preset, reset
  Multiplexer #(.select(2)) multiplexer_4 (
    .in1(A4), .in2(A6), .in3(A6), .out(multiplexer_4_out), .sel(S1_S0));  // open: in0
  D_Flip_Flop #(.trigger("falling")) d_ff_3 (.D(multiplexer_4_out), .clk(CLK_out), .Q(A5));  // open: Qn, preset, reset
  Multiplexer #(.select(2)) multiplexer_5 (
    .in1(A3), .in2(A5), .in3(A5), .out(multiplexer_5_out), .sel(S1_S0));  // open: in0
  D_Flip_Flop #(.trigger("falling")) d_ff_4 (.D(multiplexer_5_out), .clk(CLK_out), .Q(A4));  // open: Qn, preset, reset
  Multiplexer #(.select(2)) multiplexer_6 (
    .in1(A2), .in2(A4), .in3(A4), .out(multiplexer_6_out), .sel(S1_S0));  // open: in0
  D_Flip_Flop #(.trigger("falling")) d_ff_5 (.D(multiplexer_6_out), .clk(CLK_out), .Q(A3));  // open: Qn, preset, reset
  Multiplexer #(.select(2)) multiplexer_7 (
    .in1(A1), .in2(A3), .in3(A3), .out(multiplexer_7_out), .sel(S1_S0));  // open: in0
  D_Flip_Flop #(.trigger("falling")) d_ff_6 (.D(multiplexer_7_out), .clk(CLK_out), .Q(A2));  // open: Qn, preset, reset
  Multiplexer #(.select(2)) multiplexer_8 (
    .in1(A0), .in2(A2), .in3(A2), .out(multiplexer_8_out), .sel(S1_S0));  // open: in0
  D_Flip_Flop #(.trigger("falling")) d_ff_7 (.D(multiplexer_8_out), .clk(CLK_out), .Q(A1));  // open: Qn, preset, reset
  D_Flip_Flop #(.trigger("falling")) d_ff_8 (.D(multiplexer_9_out), .clk(CLK_out), .Q(A0));  // open: Qn, preset, reset
  Multiplexer #(.select(2)) multiplexer_9 (
    .in1(multiplexer_10_out), .in2(A1), .in3(A1), .out(multiplexer_9_out), .sel(S1_S0));  // open: in0
  Multiplexer #(.select(2)) multiplexer_10 (.in1(B_IN), .out(multiplexer_10_out), .sel(S1_S0));  // open: in0, in2, in3
  Multiplexer #(.select(2)) multiplexer_11 (.in1(A7), .in2(A0), .out(B_OUT), .sel(S1_S0));  // open: in0, in3
  Clock CLK (.out(CLK_out));
endmodule
